# Fritzing sketch scheme (saved by Fritzing 0.9.3b)
breadboards: 1

parts:
  U1 = NodeMCU V1.0
  YwRobot_Power_Supply1 = YwRobot Breadboard Power Supply [part_number=545043]
  LCM1602_IIC1 = LCM1602 IIC [part_number="LCM1602 IIC" chip_label="LCM1602 IIC" package="DIP (Dual Inline) [THT]"]
  ZS-042_RTC1 = ZS-042 RTC Module
  R1 = Resistor [tolerance=±5% resistance=220 package="0805 [SMD]"]
  R2 = Resistor [tolerance=±5% resistance=220 package="0805 [SMD]"]
  R3 = Resistor [tolerance=±5% resistance=220 package="0805 [SMD]"]
  LED1 = RGB LED (com. cathode, rbg) [package="5 mm [THT]"]  # not connected
  U4 = LCD-16X2 [package=lcd-16x2]

nets:
  N1: U1.D1, LCM1602_IIC1.SCL, ZS-042_RTC1.SCL
  N2: U1.D2, LCM1602_IIC1.SDA, ZS-042_RTC1.SDA
  GND: U1.GND, YwRobot_Power_Supply1.GND#13, YwRobot_Power_Supply1.GND#14, LCM1602_IIC1.GND, ZS-042_RTC1.GND
  N3: U1.D5, R1.Pin_1
  N4: U1.D6, R2.Pin_1
  N5: U1.D7, R3.Pin_1
  N6: YwRobot_Power_Supply1.VCC#5, YwRobot_Power_Supply1.VCC#6
  VCC: YwRobot_Power_Supply1.VCC#9, YwRobot_Power_Supply1.VCC#10, LCM1602_IIC1.VCC, ZS-042_RTC1.VCC
  N7: YwRobot_Power_Supply1.GND#11, YwRobot_Power_Supply1.GND#12
  VSS: LCM1602_IIC1.VSS, U4.VSS
  VDD: LCM1602_IIC1.VDD, U4.VDD
  N8: LCM1602_IIC1.V0, U4.VO
  N9: LCM1602_IIC1.RS, U4.RS
  N10: LCM1602_IIC1.RW, U4.R_W
  N11: LCM1602_IIC1.E, U4.E
  N12: LCM1602_IIC1.D0, U4.DB0
  N13: LCM1602_IIC1.D1, U4.DB1
  N14: LCM1602_IIC1.D2, U4.DB2
  N15: LCM1602_IIC1.D3, U4.DB3
  N16: LCM1602_IIC1.D4, U4.DB4
  N17: LCM1602_IIC1.D5, U4.DB5
  N18: LCM1602_IIC1.D6, U4.DB6
  N19: LCM1602_IIC1.D7, U4.DB7
  N20: LCM1602_IIC1.A, U4.A
  N21: LCM1602_IIC1.K, U4.K
  N22: LCM1602_IIC1.LED_A, LCM1602_IIC1.LED_B

custom parts:
  NodeMCU V1.0: ESP8266 based NodeMCU
  YwRobot Breadboard Power Supply: The YwRobot Breadboard Power Supply (MB-V2) has two power rails; they can be 5V or 3V3. Power to the module can be provided through the female USB socket or through the A10 (female) 2.1mm power jack.
  LCM1602 IIC: I2C-Module to use a 1602 or 2004 LCD on with the wire.h libory Serial LCD Modul
